# Fritzing sketch lidar-pcb1 (saved by Fritzing 0.9.3b)
circuit board: 5cm x 5cm
breadboards: 1

parts:
  Part1 = Arduino Nano (Rev3.0) (ICSP)
  Pololu_A1 = Pololu A4988 [package=SO16]
  J2 = screw terminal, 3 pins
  J3 = screw terminal, 4 pins
  C3 = Electrolytic Capacitor [capacitance=100µF package="100 mil [THT, electrolytic]"]
  Q1 = Basic FET P-Channel [package="TO220 [THT]"]
  C4 = Ceramic Capacitor [capacitance=100nF package="100 mil [THT, multilayer]"]  # not connected
  C5 = Ceramic Capacitor [capacitance=100nF package="100 mil [THT, multilayer]"]
  JP1 = Header 2 [package=screwterminal-3.5mm-2_lock]
  J4 = screw terminal, 5 pins
  JP2 = Header 2 [package=screwterminal-3.5mm-2_lock]
  C6 = Electrolytic Capacitor [capacitance=1µF package="100 mil [THT, electrolytic]"]

nets (from the pcb view):
  N1: Part1.GND, Pololu_A1.GND#8, JP2.2, C6.+
  N2: Part1.D2, Pololu_A1.DIR
  N3: Part1.D3, Pololu_A1.STEP
  N4: Part1.D4, Pololu_A1.ENABLE
  5V: Part1.5V, Pololu_A1.VDD, J2.pin3, JP2.1, C6.-
  N5: Part1.A5, J4.pin4
  N6: Part1.A4, J4.pin5
  N7: Pololu_A1.RESET, Pololu_A1.SLEEP
  N8: Pololu_A1.1B, J3.pin4
  N9: Pololu_A1.1A, J3.pin3
  N10: Pololu_A1.2A, J3.pin2
  N11: Pololu_A1.2B, J3.pin1
  N12: Pololu_A1.GND#14, Pololu_A1.VMOT, J2.pin1, J2.pin2, C3.-, C3.+, Q1.gate, Q1.drain, C5.0, JP1.1, JP1.2
  N13: Q1.source, C5.1
